# Fritzing sketch BedNightLight (saved by Fritzing 0.9.3b)
breadboards: 1

parts:
  U1 = NodeMCU V1.0
  R1 = PHOTOCELL [package=photocell-kit]
  R2 = Resistor [tolerance=±5% resistance=220 package="1206 [SMD]"]
  PIR1 = PIR sensor
  NEOPIXEL1 = Neopixel Strip -- Black (30/m)

nets:
  N1: U1.D2, NEOPIXEL1.DI
  N2: U1.D6, PIR1.SIG
  N3: U1.A0, R1.P$1, R2.Pin_0
  5V: R1.P$2, PIR1.VDD, NEOPIXEL1.+5V
  GND: R2.Pin_1, PIR1.GND, NEOPIXEL1.GND

custom parts:
  NodeMCU V1.0: ESP8266 based NodeMCU
  Neopixel Strip -- Black (30/m): Neopixel Strip, Black, 30 pixels per meter.
