# Fritzing sketch ArduinoMultiShiftRegister (saved by Fritzing 0.9.3b)
breadboards: 1

parts:
  Part1 = Arduino Uno (Rev3)
  U1 = 16-Channel Relay Module [package=relay-16ch]
  U2 = 74HC595 SMD [package="SO16 [SMD]"]
  U3 = 74HC595 SMD [package="SO16 [SMD]"]

nets:
  N1: Part1.D2, U3.DS
  N2: Part1.D3_PWM, U2.ST_CP, U3.ST_CP
  N3: Part1.D4, U2.SH_CP, U3.SH_CP
  N4: U1.IN1, U3.Q0
  N5: U1.IN2, U3.Q1
  N6: U1.IN3, U3.Q2
  N7: U1.IN4, U3.Q3
  N8: U1.IN5, U3.Q4
  N9: U1.IN6, U3.Q5
  N10: U1.IN7, U3.Q6
  N11: U1.IN8, U3.Q7
  N12: U1.IN9, U2.Q0
  N13: U1.IN10, U2.Q1
  N14: U1.IN11, U2.Q2
  N15: U1.IN12, U2.Q3
  N16: U1.IN13, U2.Q4
  N17: U1.IN14, U2.Q5
  N18: U1.IN15, U2.Q6
  N19: U1.IN16, U2.Q7
  GND: U1.OUT_GND, U2.GND, U3.GND
  VCC: U2.MR, U2.VCC, U3.MR, U3.VCC
  N20: U2.DS, U3.Q7'

custom parts:
  16-Channel Relay Module: 16 channel relay module
