# Fritzing sketch 8portRelay (saved by Fritzing 0.9.3b)
breadboards: 1

parts:
  Part1 = Arduino Uno (Rev3)
  V1 = DC Power [voltage=5]  # not connected
  U1 = 16-Channel Relay Module [package=relay-16ch]

nets (from the breadboard view):
  N1: Part1.D8, U1.IN7
  N2: Part1.D9_PWM, U1.IN8
  N3: Part1.D2, U1.IN1
  N4: Part1.D3_PWM, U1.IN2
  N5: Part1.D4, U1.IN3
  N6: Part1.D5_PWM, U1.IN4
  N7: Part1.D6_PWM, U1.IN5
  N8: Part1.D7, U1.IN6
  N9: Part1.GND, U1.OUT_GND
  N10: Part1.VIN, U1.VCCOUT_5V

custom parts:
  16-Channel Relay Module: 16 channel relay module
