# Fritzing sketch ESP32WithShiftRegisters (saved by Fritzing 0.9.3b)
circuit board: 7.6cm x 10cm
breadboards: 2

parts:
  74595-1 = 74HC595 [package="DIP16 [THT]"]
  74595-2 = 74HC595 [package="DIP16 [THT]"]
  12V_IN = female pin header, 2 pins [form="♀ (female)"]
  GND = female pin header, 2 pins [form="♀ (female)"]
  12V = female pin header, 2 pins [form="♀ (female)"]
  7805_5V_Reg = Voltage Regulator [package=78xxl]
  Relays_1-8 = female pin header, 8 pins [form="♀ (female)"]
  Relays_9-16 = female pin header, 8 pins [form="♀ (female)"]
  ESP32-S = female pin header, 15 pins [form="♀ (female)"]
  ESP32-S_2 = female pin header, 15 pins [form="♀ (female)"]
  U1 = ESP32S-30Pin [part_number=ESP32S-Generic]

nets:
  N1: 74595-1.Q1, Relays_1-8.pin7
  N2: 74595-1.Q2, Relays_1-8.pin6
  N3: 74595-1.Q3, Relays_1-8.pin5
  N4: 74595-1.Q4, Relays_1-8.pin4
  N5: 74595-1.Q5, Relays_1-8.pin3
  N6: 74595-1.Q6, Relays_1-8.pin2
  N7: 74595-1.Q7, Relays_1-8.pin1
  GND: 74595-1.GND, 74595-1.OE, 74595-2.GND, 74595-2.OE, 12V_IN.pin2, GND.pin2, 12V.pin2, 7805_5V_Reg.GND, ESP32-S.pin2, ESP32-S_2.pin2, U1.GND
  N8: 74595-1.Q7', 74595-2.DS
  VCC: 74595-1.MR, 74595-1.VCC, 74595-2.MR, 74595-2.VCC, 7805_5V_Reg.OUT
  N9: 74595-1.SH_CP, 74595-2.SH_CP, ESP32-S_2.pin6, U1.GPIO27
  N10: 74595-1.ST_CP, 74595-2.ST_CP, ESP32-S_2.pin7, U1.GPIO26
  N11: 74595-1.DS, ESP32-S_2.pin8, U1.GPIO25
  N12: 74595-1.Q0, Relays_1-8.pin8
  N13: 74595-2.Q1, Relays_9-16.pin7
  N14: 74595-2.Q2, Relays_9-16.pin6
  N15: 74595-2.Q3, Relays_9-16.pin5
  N16: 74595-2.Q4, Relays_9-16.pin4
  N17: 74595-2.Q5, Relays_9-16.pin3
  N18: 74595-2.Q6, Relays_9-16.pin2
  N19: 74595-2.Q7, Relays_9-16.pin1
  N20: 74595-2.Q0, Relays_9-16.pin8
  N21: 12V_IN.pin1, GND.pin1, 12V.pin1, 7805_5V_Reg.IN, ESP32-S_2.pin1, U1.VIN
  N22: ESP32-S.pin1, U1.3.3
  N23: ESP32-S.pin3, U1.GPIO15
  N24: ESP32-S.pin4, U1.GPIO2
  N25: ESP32-S.pin5, U1.GPIO4
  N26: ESP32-S.pin6, U1.RX2
  N27: ESP32-S.pin7, U1.TX2
  N28: ESP32-S.pin8, U1.GPIO5
  N29: ESP32-S.pin9, U1.GPIO18
  N30: ESP32-S.pin10, U1.GPIO19
  N31: ESP32-S.pin11, U1.GPIO21
  N32: ESP32-S.pin12, U1.RX0
  N33: ESP32-S.pin13, U1.TX0
  N34: ESP32-S.pin14, U1.GPIO22
  N35: ESP32-S.pin15, U1.GPIO23
  N36: ESP32-S_2.pin3, U1.GPIO13
  N37: ESP32-S_2.pin4, U1.GPIO12
  N38: ESP32-S_2.pin5, U1.GPIO14
  N39: ESP32-S_2.pin9, U1.GPIO33
  N40: ESP32-S_2.pin10, U1.GPIO32
  N41: ESP32-S_2.pin11, U1.GPIO35
  N42: ESP32-S_2.pin12, U1.GPIO34
  N43: ESP32-S_2.pin13, U1.VN
  N44: ESP32-S_2.pin14, U1.VP
  N45: ESP32-S_2.pin15, U1.EN

custom parts:
  ESP32S-30Pin: ESP-WROOM-32 ESP32 ESP-32S Development Board 2.4GHz Dual-Mode WiFi + Bluetooth Dual Cores Microcontroller The ESP32 integrated with Antenna switches, RF Balun, power amplifiers, low-noise amplifiers, filters, and management modules, and the entire solution occupies the least area of PCB. 2.4 GHz Wi-Fi plus Bluetooth dual-mode chip, with TSMC Ultra-low power consumption 40nm technology, power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
